// Logisim project 1.circ as structural Verilog: 1 circuit, main circuit main
module main (
  input  [3:0] A,
  input  [3:0] B,
  output [7:0] out_3,
  output [2:0] o0,
  output [2:0] o1,
  output [2:0] o2,
  output [7:0] out_7
);

  ROM #(.addrWidth(4)) rom_1 (.addr(B), .data(out_7));
  // Probe on A
  // Probe on B
  // Probe on A
  // Probe on B
  // Probe on {A, B}
  // Probe on {A, B}
  // Probe on out_7
  // Probe on {A, B}
  // Probe on B[2:0]
  // Probe on {A[1:0], B[3]}
  // Probe on A[3:2]

  assign o0 = B[2:0];
  assign o1 = {A[1:0], B[3]};
  assign o2 = {1'b0, A[3:2]};
  assign out_3 = {A, B};

  // Other names for the same wires on the sheet: temp[7:0] = {A, B}

  // Notes on the sheet:
  //   contents of rom_1 (hex, n*v repeats v):
  //   4a 3b 2c 1d
endmodule
