// Logisim project 2.circ as structural Verilog: 1 circuit, main circuit main
module main (
  input  [3:0] a,
  input  [3:0] b,
  output [3:0] out_3,
  output [3:0] out_4,
  output [7:0] out_5,
  output [4:0] out_6,
  output [3:0] out_7,
  output out_8,
  output [4:0] out_9
);

  wire adder_2_cout, adder_3_cout, adder_4_cout;

  // Probe on a
  // Probe on b
  Adder #(.width(1)) adder_1 (.a(a[3]), .b(b[3]), .out(out_6[3]), .cin(adder_2_cout), .cout(out_6[4]));
  xor xor_1 (out_8, out_6[4], adder_2_cout);
  Adder #(.width(1)) adder_2 (.a(a[2]), .b(b[2]), .out(out_6[2]), .cin(adder_3_cout), .cout(adder_2_cout));
  Adder #(.width(1)) adder_3 (.a(a[1]), .b(b[1]), .out(out_6[1]), .cin(adder_4_cout), .cout(adder_3_cout));
  Adder #(.width(1)) adder_4 (.a(a[0]), .b(b[0]), .out(out_6[0]), .cin(1'b0), .cout(adder_4_cout));
  // Probe on out_6
  // Probe on out_6[3:0]
  // Probe on out_6
  Adder adder_5 ();  // open: a, b, out, cin, cout

  assign out_3 = a;
  assign out_4 = {4{a[3]}};
  assign out_5 = {{5{a[3]}}, a[2:0]};
  assign out_7 = out_6[3:0];
  assign out_9 = out_6;

  // Other names for the same wires on the sheet: temp[3:0] = a
endmodule
