// Logisim project 4.circ as structural Verilog: 2 circuits, main circuit comp
module comp (
  input  [3:0] a,
  input  [3:0] b,
  output [3:0] x,
  output [3:0] y
);

  wire comparator_1_gt;

  // Probe on b
  // Probe on a
  Comparator #(.mode("unsigned"), .width(4)) comparator_1 (.a(a), .b(b), .gt(comparator_1_gt));  // open: eq, lt
  // Probe on x
  Multiplexer #(.width(4)) multiplexer_1 (.in0(a), .in1(b), .out(x), .sel(comparator_1_gt));
  Multiplexer #(.width(4)) multiplexer_2 (.in0(b), .in1(a), .out(y), .sel(comparator_1_gt));
  // Probe on y
endmodule

module sn (
  input  [3:0] a,
  input  [3:0] b,
  input  [3:0] c,
  input  [3:0] d,
  output [3:0] x,
  output [3:0] y,
  output [3:0] w,
  output [3:0] z
);

  wire [3:0] b0_x, b0_y, b1_x, b1_y, b2_y, b3_x;

  comp b0 (.a(a), .b(c), .x(b0_x), .y(b0_y));
  comp b1 (.a(b), .b(d), .x(b1_x), .y(b1_y));
  comp b2 (.a(b0_x), .b(b1_x), .x(x), .y(b2_y));
  comp b3 (.a(b0_y), .b(b1_y), .x(b3_x), .y(z));
  comp b4 (.a(b2_y), .b(b3_x), .x(y), .y(w));
endmodule
