// Logisim project Lab11_RAM_JC.circ as structural Verilog: 1 circuit, main circuit main
module main (
);

  wire and_1_out, and_2_out, clk, clr_out, rd, rd_wrt_out, Reset_out, wrt;
  wire [6:0] keyboard_1_data;
  wire [7:0] controlled_buffer_2_out, counter_1_q, ram_1_data;

  Button Reset (.out(Reset_out));
  Counter counter_1 (.clr(Reset_out), .clk(clk), .Q(counter_1_q));  // open: load, up, count, D, carry
  T_Flip_Flop t_ff_1 (.T(1'b1), .clk(rd_wrt_out), .Q(wrt), .Qn(rd));  // open: reset, preset
  Button rd_wrt (.out(rd_wrt_out));
  Button u_clk (.out(clk));
  LED Read_from_RAM (.in(rd));
  LED Write_to_RAM (.in(wrt));
  RAM #(.asyncread("true"), .clearpin("true"), .databus("bidir")) ram_1 (
    .addr(counter_1_q), .we(wrt), .oe(rd), .clk(clk), .data(ram_1_data));  // open: clr
  and and_1 (and_1_out, clk, wrt);
  assign ram_1_data = wrt ? {1'b0, keyboard_1_data} : 8'bz;  // Controlled_Buffer controlled_buffer_1
  assign controlled_buffer_2_out = rd ? ram_1_data : 8'bz;  // Controlled_Buffer controlled_buffer_2
  Keyboard #(.buflen(64)) keyboard_1 (.clk(and_1_out), .data(keyboard_1_data));  // open: re, clr, avail
  and and_2 (and_2_out, clk, rd);
  TTY tty_1 (.data(controlled_buffer_2_out[6:0]), .clk(and_2_out), .clr(clr_out));  // open: we
  Button clr (.out(clr_out));

  // Notes on the sheet:
  //   Name:
  //   Lab 10: RAM
  //   Date
  //   Jan Czechowski
  //   26.05.2025
endmodule
