// Logisim project peas.circ as structural Verilog: 7 circuits, main circuit main
module main (
  input  mode
);

  wire clk_out;
  wire [2:0] aut_1_ps;
  wire [6:0] H0, H1, H2, H3;

  _7_Segment_Display u_7_segment_display_1 (
    .g(H3[6]), .f(H3[5]), .a(H3[0]), .b(H3[1]), .e(H3[4]), .d(H3[3]), .c(H3[2]));  // open: dp
  _7_Segment_Display u_7_segment_display_2 (
    .g(H2[6]), .f(H2[5]), .a(H2[0]), .b(H2[1]), .e(H2[4]), .d(H2[3]), .c(H2[2]));  // open: dp
  Clock clk (.out(clk_out));
  _7_Segment_Display u_7_segment_display_3 (
    .g(H1[6]), .f(H1[5]), .a(H1[0]), .b(H1[1]), .e(H1[4]), .d(H1[3]), .c(H1[2]));  // open: dp
  _7_Segment_Display u_7_segment_display_4 (
    .g(H0[6]), .f(H0[5]), .a(H0[0]), .b(H0[1]), .e(H0[4]), .d(H0[3]), .c(H0[2]));  // open: dp
  // Probe on aut_1_ps
  aut aut_1 (.mode(mode), .clk(clk_out), .PS(aut_1_ps));
  d_H0 d_h0_1 (.PS(aut_1_ps), .a(H0[0]), .b(H0[1]), .c(H0[2]), .d(H0[3]), .e(H0[4]), .f(H0[5]), .g(H0[6]));
  d_H1 d_h1_1 (.PS(aut_1_ps), .a(H1[0]), .b(H1[1]), .c(H1[2]), .d(H1[3]), .e(H1[4]), .f(H1[5]), .g(H1[6]));
  d_H2 d_h2_1 (.PS(aut_1_ps), .a(H2[0]), .b(H2[1]), .c(H2[2]), .d(H2[3]), .e(H2[4]), .f(H2[5]), .g(H2[6]));
  d_H3 d_h3_1 (.PS(aut_1_ps), .a(H3[0]), .b(H3[1]), .c(H3[2]), .d(H3[3]), .e(H3[4]), .f(H3[5]), .g(H3[6]));
endmodule

module aut (
  input  mode,
  input  clk,
  output [2:0] PS
);

  wire ns_1_d0, ns_1_d1, ns_1_d2;

  NS ns_1 (.Q0(PS[0]), .Q1(PS[1]), .Q2(PS[2]), .mode(mode), .D0(ns_1_d0), .D1(ns_1_d1), .D2(ns_1_d2));
  D_Flip_Flop DFF2 (.D(ns_1_d2), .clk(clk), .Q(PS[2]));  // open: Qn, preset, reset
  D_Flip_Flop DFF1 (.D(ns_1_d1), .clk(clk), .Q(PS[1]));  // open: Qn, preset, reset
  D_Flip_Flop DFF0 (.D(ns_1_d0), .clk(clk), .Q(PS[0]));  // open: Qn, preset, reset
endmodule

module NS (
  input  Q0,
  input  Q1,
  input  Q2,
  input  mode,
  output D0,
  output D1,
  output D2
);

  Adder #(.width(3)) adder_1 (.a({Q2, Q1, Q0}), .b({2'b00, mode}), .out({D2, D1, D0}));  // open: cin, cout
endmodule

module d_H0 (
  input  [2:0] PS,
  output a,
  output b,
  output c,
  output d,
  output e,
  output f,
  output g
);

  wire and_4_out, and_5_out, not_2_out, not_3_out;

  not not_1 (a, PS[2]);
  not not_2 (not_2_out, PS[1]);
  not not_3 (not_3_out, PS[0]);
  and and_1 (b, a, not_3_out);
  and and_2 (c, a, PS[1]);
  and and_3 (d, a, PS[0]);
  and and_4 (and_4_out, a, not_2_out);
  and and_5 (and_5_out, a, not_3_out);
  or or_1 (e, and_4_out, and_5_out);

  assign f = a;
  assign g = a;
endmodule

module d_H1 (
  input  [2:0] PS,
  output a,
  output b,
  output c,
  output d,
  output e,
  output f,
  output g
);

  wire and_1_out, and_2_out, and_3_out, and_5_out, and_6_out, and_7_out, and_8_out, and_9_out, and_10_out,
       and_11_out, and_12_out, and_13_out, and_14_out, and_15_out, and_16_out, not_1_out, not_2_out,
       not_3_out;

  not not_1 (not_1_out, PS[2]);
  not not_2 (not_2_out, PS[1]);
  not not_3 (not_3_out, PS[0]);
  and and_1 (and_1_out, not_1_out, PS[0]);
  and and_2 (and_2_out, not_1_out, PS[1]);
  and and_3 (and_3_out, PS[2], not_2_out, not_3_out);
  and and_4 (b, not_1_out, PS[0]);
  and and_5 (and_5_out, not_1_out, PS[1], PS[0]);
  and and_6 (and_6_out, PS[2], not_2_out, not_3_out);
  and and_7 (and_7_out, not_1_out, PS[1], not_3_out);
  and and_8 (and_8_out, PS[2], not_2_out, not_3_out);
  and and_9 (and_9_out, not_1_out, PS[0]);
  and and_10 (and_10_out, not_1_out, PS[1]);
  and and_11 (and_11_out, not_1_out, PS[0]);
  and and_12 (and_12_out, not_1_out, PS[1]);
  and and_13 (and_13_out, PS[2], not_2_out, not_3_out);
  and and_14 (and_14_out, not_1_out, PS[0]);
  and and_15 (and_15_out, not_1_out, PS[1]);
  and and_16 (and_16_out, PS[2], not_2_out, not_3_out);
  or or_1 (a, and_1_out, and_2_out, and_3_out);
  or or_2 (c, and_5_out, and_6_out);
  or or_3 (d, and_7_out, and_8_out);
  or or_4 (e, and_9_out, and_10_out);
  or or_5 (f, and_11_out, and_12_out, and_13_out);
  or or_6 (g, and_14_out, and_15_out, and_16_out);
endmodule

module d_H2 (
  input  [2:0] PS,
  output a,
  output b,
  output c,
  output d,
  output e,
  output f,
  output g
);

  wire and_1_out, and_2_out, and_3_out, and_4_out, and_6_out, and_7_out, and_8_out, and_9_out, and_10_out,
       and_11_out, and_12_out, and_13_out, not_1_out, not_2_out, not_3_out;

  not not_1 (not_1_out, PS[2]);
  not not_2 (not_2_out, PS[1]);
  not not_3 (not_3_out, PS[0]);
  and and_1 (and_1_out, not_1_out, PS[1]);
  and and_2 (and_2_out, PS[2], not_2_out);
  and and_3 (and_3_out, not_1_out, PS[1], not_3_out);
  and and_4 (and_4_out, PS[2], not_2_out, not_3_out);
  and and_5 (c, PS[2], not_2_out);
  and and_6 (and_6_out, not_1_out, PS[1], PS[0]);
  and and_7 (and_7_out, PS[2], not_2_out, PS[0]);
  and and_8 (and_8_out, not_1_out, PS[1]);
  and and_9 (and_9_out, PS[2], not_2_out, not_3_out);
  and and_10 (and_10_out, not_1_out, PS[1]);
  and and_11 (and_11_out, PS[2], not_2_out);
  and and_12 (and_12_out, not_1_out, PS[1]);
  and and_13 (and_13_out, PS[2], not_2_out);
  or or_1 (a, and_1_out, and_2_out);
  or or_2 (b, and_3_out, and_4_out);
  or or_3 (d, and_6_out, and_7_out);
  or or_4 (e, and_8_out, and_9_out);
  or or_5 (f, and_10_out, and_11_out);
  or or_6 (g, and_12_out, and_13_out);
endmodule

module d_H3 (
  input  [2:0] PS,
  output a,
  output b,
  output c,
  output d,
  output e,
  output f,
  output g
);

  wire and_1_out, and_2_out, and_3_out, and_4_out, and_5_out, and_6_out, and_7_out, and_9_out, and_10_out,
       and_11_out, and_12_out, and_13_out, and_14_out, and_15_out, and_16_out, not_1_out, not_2_out,
       not_3_out;

  not not_1 (not_1_out, PS[2]);
  not not_2 (not_2_out, PS[1]);
  not not_3 (not_3_out, PS[0]);
  and and_1 (and_1_out, not_1_out, PS[1], PS[0]);
  and and_2 (and_2_out, PS[2], not_2_out);
  and and_3 (and_3_out, PS[2], not_3_out);
  and and_4 (and_4_out, not_1_out, PS[1], PS[0]);
  and and_5 (and_5_out, PS[2], not_2_out, PS[0]);
  and and_6 (and_6_out, PS[2], not_2_out, PS[0]);
  and and_7 (and_7_out, PS[2], PS[1], not_3_out);
  and and_8 (d, PS[2], not_3_out);
  and and_9 (and_9_out, not_1_out, PS[1], PS[0]);
  and and_10 (and_10_out, PS[2], not_2_out);
  and and_11 (and_11_out, not_1_out, PS[1], PS[0]);
  and and_12 (and_12_out, PS[2], not_2_out);
  and and_13 (and_13_out, PS[2], not_3_out);
  and and_14 (and_14_out, not_1_out, PS[1], PS[0]);
  and and_15 (and_15_out, PS[2], not_2_out);
  and and_16 (and_16_out, PS[2], not_3_out);
  or or_1 (a, and_1_out, and_2_out, and_3_out);
  or or_2 (b, and_4_out, and_5_out);
  or or_3 (c, and_6_out, and_7_out);
  or or_4 (e, and_9_out, and_10_out);
  or or_5 (f, and_11_out, and_12_out, and_13_out);
  or or_6 (g, and_14_out, and_15_out, and_16_out);
endmodule
