// Logisim project lab3.circ as structural Verilog
module rockmore (
  input  C,
  input  L,
  input  A,
  input  R,
  output M
);

  wire and_1_out, and_2_out, not_1_out, not_2_out, not_3_out, or_1_out;

  not not_1 (not_1_out, C);
  not not_2 (not_2_out, R);
  or or_1 (or_1_out, not_1_out, L);
  and and_1 (and_1_out, or_1_out, A);
  and and_2 (and_2_out, A, not_2_out);
  not not_3 (not_3_out, and_2_out);
  xor xor_1 (M, and_1_out, not_3_out);
endmodule

module exactlyone (
  input  A,
  input  B,
  input  C,
  output P
);

  wire and_1_out, and_2_out, and_3_out, not_1_out, not_2_out, not_3_out;

  not not_1 (not_1_out, A);
  not not_2 (not_2_out, B);
  not not_3 (not_3_out, C);
  and and_1 (and_1_out, not_1_out, not_2_out, C);
  and and_2 (and_2_out, not_1_out, B, not_3_out);
  or or_1 (P, and_1_out, and_2_out, and_3_out);
  and and_3 (and_3_out, A, not_2_out, not_3_out);
endmodule

module election (
  input  [3:0] N,
  output H,
  output L,
  output T
);

  wire and_1_out, and_2_out, and_3_out, and_4_out, and_5_out, and_6_out, and_7_out, and_8_out, and_9_out,
       and_10_out, and_11_out, and_12_out, and_13_out, and_14_out, not_1_out, not_2_out, not_3_out, not_4_out;

  not not_1 (not_1_out, N[3]);
  not not_2 (not_2_out, N[2]);
  not not_3 (not_3_out, N[1]);
  not not_4 (not_4_out, N[0]);
  and and_1 (and_1_out, N[2], N[1], N[0]);
  and and_2 (and_2_out, N[3], N[1], N[0]);
  and and_3 (and_3_out, N[3], N[2], N[0]);
  and and_4 (and_4_out, N[3], N[2], N[1]);
  and and_5 (and_5_out, not_1_out, not_2_out, not_3_out);
  and and_6 (and_6_out, not_1_out, not_2_out, not_4_out);
  and and_7 (and_7_out, not_1_out, not_3_out, not_4_out);
  and and_8 (and_8_out, not_2_out, not_3_out, not_4_out);
  and and_9 (and_9_out, not_1_out, not_2_out, N[1], N[0]);
  and and_10 (and_10_out, not_1_out, N[2], not_3_out, N[0]);
  and and_11 (and_11_out, not_1_out, N[2], N[1], not_4_out);
  and and_12 (and_12_out, N[3], not_2_out, not_3_out, N[0]);
  and and_13 (and_13_out, N[3], not_2_out, N[1], not_4_out);
  and and_14 (and_14_out, N[3], N[2], not_3_out, not_4_out);
  or or_1 (H, and_1_out, and_2_out, and_3_out, and_4_out);
  or or_2 (L, and_5_out, and_6_out, and_7_out, and_8_out);
  or or_3 (T, and_9_out, and_10_out, and_11_out, and_12_out, and_13_out, and_14_out);
endmodule

module onehot (
  input  [1:0] N,
  output A,
  output B,
  output C,
  output D
);

  wire not_1_out, not_2_out;

  not not_1 (not_1_out, N[0]);
  not not_2 (not_2_out, N[1]);
  and and_1 (A, not_1_out, not_2_out);
  and and_2 (B, N[0], not_2_out);
  and and_3 (C, not_1_out, N[1]);
  and and_4 (D, N[0], N[1]);
endmodule

module grid4x4 (
  input  [3:0] T
);

  wire and_1_out, and_2_out, and_3_out, and_4_out, not_1_out, not_2_out, not_3_out, not_4_out, rgbled_2_p1,
       rgbled_3_p1, rgbled_5_p1, rgbled_6_p1;

  not not_1 (not_1_out, T[0]);
  and and_1 (and_1_out, not_1_out, not_2_out);
  not not_2 (not_2_out, T[1]);
  and and_2 (and_2_out, T[0], T[1]);
  not not_3 (not_3_out, T[3]);
  not not_4 (not_4_out, T[2]);
  and and_3 (and_3_out, not_3_out, not_4_out);
  // RGBLED rgbled_1: pin names not known
  // RGBLED rgbled_2: pin names not known; wires that end beside it: rgbled_2_p1
  // RGBLED rgbled_3: pin names not known; wires that end beside it: rgbled_3_p1
  // RGBLED rgbled_4: pin names not known; wires that end beside it: and_3_out
  // RGBLED rgbled_5: pin names not known; wires that end beside it: rgbled_5_p1
  // RGBLED rgbled_6: pin names not known; wires that end beside it: rgbled_6_p1
  // RGBLED rgbled_7: pin names not known
  // RGBLED rgbled_8: pin names not known
  // RGBLED rgbled_9: pin names not known
  // RGBLED rgbled_10: pin names not known
  // RGBLED rgbled_11: pin names not known; wires that end beside it: rgbled_5_p1
  // RGBLED rgbled_12: pin names not known; wires that end beside it: rgbled_6_p1
  and and_4 (and_4_out, T[3], T[2]);
  // RGBLED rgbled_13: pin names not known; wires that end beside it: and_1_out
  // RGBLED rgbled_14: pin names not known; wires that end beside it: rgbled_2_p1
  // RGBLED rgbled_15: pin names not known; wires that end beside it: rgbled_3_p1
  // RGBLED rgbled_16: pin names not known; wires that end beside it: and_4_out, and_2_out

  // Notes on the sheet:
  //   4
  //   0
  //   1
  //   2
  //   3
  //   8
  //   5
  //   9
  //   6
  //   a
  //   7
  //   b
  //   c
  //   d
  //   e
  //   f
endmodule

module display (
  input  [4:0] in_1,
  input  [4:0] in_2,
  input  [4:0] in_3,
  input  [4:0] in_4,
  input  [4:0] in_5,
  input  [4:0] in_6,
  input  [4:0] in_7,
  input  [4:0] in_8,
  input  [4:0] in_9,
  input  I_N,
  input  [4:0] in_11,
  input  [4:0] in_12,
  input  [4:0] in_13
);

  wire [4:0] multiplexer_1_out, multiplexer_2_out, multiplexer_3_out, multiplexer_4_out;

  DotMatrix #(.matrixcols(4), .matrixrows(5)) dotmatrix_1 (.col0(in_3), .col1(in_5), .col2(in_7), .col3(in_9));
  DotMatrix #(.matrixcols(4), .matrixrows(5)) dotmatrix_2 (
    .col0(multiplexer_1_out), .col1(multiplexer_2_out), .col2(multiplexer_3_out), .col3(multiplexer_4_out));
  Multiplexer #(.width(5)) multiplexer_1 (.in0(in_1), .in1(in_2), .out(multiplexer_1_out), .sel(I_N));
  Multiplexer #(.width(5)) multiplexer_2 (.in0(in_4), .in1(in_6), .out(multiplexer_2_out), .sel(I_N));
  Multiplexer #(.width(5)) multiplexer_3 (.in0(in_8), .in1(in_11), .out(multiplexer_3_out), .sel(I_N));
  Multiplexer #(.width(5)) multiplexer_4 (.in0(in_12), .in1(in_13), .out(multiplexer_4_out), .sel(I_N));
endmodule
