// Logisim project lab3_PD_JanCzechowski.circ as structural Verilog: 1 circuit, main circuit main
module main (
  input  I_N,
  input  [5:0] in_2,
  input  [5:0] in_3,
  input  [5:0] in_4,
  input  [5:0] in_5,
  input  [5:0] in_6,
  input  [5:0] in_7,
  input  [5:0] in_8,
  input  [5:0] in_9,
  input  [5:0] in_10,
  input  [5:0] in_11,
  input  [5:0] in_12,
  input  [5:0] in_13,
  input  [5:0] in_14,
  input  [5:0] in_15,
  input  [5:0] in_16,
  input  [5:0] in_17
);

  wire [5:0] multiplexer_1_out, multiplexer_2_out, multiplexer_3_out, multiplexer_4_out, multiplexer_5_out,
       multiplexer_6_out, multiplexer_7_out, multiplexer_8_out;

  Multiplexer #(.width(6)) multiplexer_1 (.in0(in_2), .in1(in_3), .out(multiplexer_1_out), .sel(I_N));
  Multiplexer #(.width(6)) multiplexer_2 (.in0(in_4), .in1(in_5), .out(multiplexer_2_out), .sel(I_N));
  Multiplexer #(.width(6)) multiplexer_3 (.in0(in_6), .in1(in_7), .out(multiplexer_3_out), .sel(I_N));
  Multiplexer #(.width(6)) multiplexer_4 (.in0(in_8), .in1(in_9), .out(multiplexer_4_out), .sel(I_N));
  Multiplexer #(.width(6)) multiplexer_5 (.in0(in_10), .in1(in_11), .out(multiplexer_5_out), .sel(I_N));
  Multiplexer #(.width(6)) multiplexer_6 (.in0(in_12), .in1(in_13), .out(multiplexer_6_out), .sel(I_N));
  Multiplexer #(.width(6)) multiplexer_7 (.in0(in_14), .in1(in_15), .out(multiplexer_7_out), .sel(I_N));
  Multiplexer #(.width(6)) multiplexer_8 (.in0(in_16), .in1(in_17), .out(multiplexer_8_out), .sel(I_N));
  DotMatrix #(.inputtype("row"), .matrixcols(6), .matrixrows(8)) dotmatrix_1 (
    .row0(multiplexer_1_out), .row1(multiplexer_2_out), .row2(multiplexer_3_out), .row3(multiplexer_4_out),
    .row4(multiplexer_5_out), .row5(multiplexer_6_out), .row6(multiplexer_7_out), .row7(multiplexer_8_out));

  // Notes on the sheet:
  //   in_3: initial=0x1f
  //   in_4: initial=0x1
  //   in_5: initial=0x20
  //   in_6: initial=0x1
  //   in_7: initial=0x20
  //   in_8: initial=0x1
  //   in_9: initial=0x20
  //   in_10: initial=0x1
  //   in_11: initial=0x20
  //   in_12: initial=0x11
  //   in_13: initial=0x20
  //   in_14: initial=0x11
  //   in_15: initial=0x20
  //   in_16: initial=0x1f
  //   in_17: initial=0x1f
  //   in_2: initial=0x3f
  //   Jan
  //   Czechowski
  //   01.04.2025
  //   POTEC 2025L  
  //   337066
endmodule
