// Logisim project lab3_PD_JanCzechowski_v2.circ as structural Verilog: 1 circuit, main circuit main
module main (
  input  in_1
);

  wire [5:5] multiplexer_1_out, not_1_out;

  Multiplexer multiplexer_1 (.in0(1'b1), .in1(1'b0), .out(multiplexer_1_out[5]), .sel(in_1));
  not not_1 (not_1_out[5], multiplexer_1_out[5]);
  DotMatrix #(.inputtype("row"), .matrixcols(6), .matrixrows(8)) dotmatrix_1 (
    .row0({multiplexer_1_out[5], {5{1'b1}}}), .row1({not_1_out[5], 4'b0000, multiplexer_1_out[5]}),
    .row2({not_1_out[5], 4'b0000, multiplexer_1_out[5]}),
    .row3({not_1_out[5], 4'b0000, multiplexer_1_out[5]}),
    .row4({not_1_out[5], 4'b0000, multiplexer_1_out[5]}),
    .row5({not_1_out[5], multiplexer_1_out[5], 3'b000, multiplexer_1_out[5]}),
    .row6({not_1_out[5], multiplexer_1_out[5], 3'b000, multiplexer_1_out[5]}), .row7(6'b011111));

  // Notes on the sheet:
  //   Jan
  //   Czechowski
  //   337066
  //   01.04.2025
  //   POTEC 2025L  
endmodule
